# Fritzing sketch gbMon2 (saved by Fritzing 0.8.3b)
breadboards: 3

parts:
  Raspberry_Pi_rev1 = Raspberry Pi rev2
  XTAL1 = Crystal [frequency="16 Mhz" package=SMD]
  Graphic_Display = single row smd male pin header, 20 pins [form="♂ (male)"]
  ICL1 = ICL7660 [chip_label=ICL7660 package="DIP (Dual Inline) [THT]"]
  atmega328P1 = atmega328P [package=dip]
  C3 = Ceramic Capacitor [capacitance=10µF voltage=16V package="100 mil [THT, multilayer]"]
  C4 = Ceramic Capacitor [capacitance=10µF voltage=16V package="100 mil [THT, multilayer]"]
  R1 = Trimmer Potentiometer [maximum_resistance=10kΩ package=THT]
  C2 = Ceramic Capacitor [capacitance=22pF package="100 mil [THT, multilayer]"]
  C1 = Ceramic Capacitor [capacitance=22pF package="100 mil [THT, multilayer]"]
  J1 = female pin header, 2 pins [form="♀ (female)"]
  S1 = Pushbutton [package="[THT]"]
  R2 = Resistor [tolerance=±5% resistance=220 package=THT]
  RF434_Transmitter = RF 434Mhz Transmitter [package=rf-link_tx]
  DHT22 = DHT22 Humidity and Temperature Sensor
  R3 = Resistor [tolerance=±5% resistance=10k package=THT]
  DS1 = DS18B20 1-Wire Temperature Sensor [part_number=DS18B20]
  R4 = Resistor [tolerance=±5% resistance=4.7k package=THT]
  DS1-5 = DS18B20 1-Wire Temperature Sensor [part_number=DS18B20]

nets:
  VDD: Raspberry_Pi_rev1.3V3, DHT22.VDD, R3.Pin_1, DS1.VDD, R4.Pin_1, DS1-5.VDD
  5V: Raspberry_Pi_rev1.5V, Graphic_Display.pin1, Graphic_Display.pin14, Graphic_Display.pin19, atmega328P1.VCC, atmega328P1.AVCC, R1.leg2, R2.Pin_1, RF434_Transmitter.+5V
  GND: Raspberry_Pi_rev1.GND, Graphic_Display.pin2, Graphic_Display.pin18, Graphic_Display.pin20, ICL1.GND, atmega328P1.GND, C4.0, R1.leg1, C2.1, C1.0, S1.Pin_3, S1.Pin_4, RF434_Transmitter.GND, DHT22.GND, DS1.GND, DS1-5.GND
  N1: Raspberry_Pi_rev1.GPIO_23, DS1.DQ, R4.Pin_0, DS1-5.DQ
  N2: Raspberry_Pi_rev1.GPIO_17, atmega328P1.D3_(PWM)
  N3: Raspberry_Pi_rev1.GPIO_18, DHT22.DATA, R3.Pin_0
  N4: Raspberry_Pi_rev1.GPIO_27, RF434_Transmitter.DATA
  N5: Raspberry_Pi_rev1.GPIO_22, atmega328P1.D2
  N6: XTAL1.pin_0, atmega328P1.XLAT1, C1.1
  N7: XTAL1.pin_1, atmega328P1.XLAT2, C2.0
  N8: Graphic_Display.pin3, ICL1.V_out, C4.1
  N9: Graphic_Display.pin4, atmega328P1.D8
  N10: Graphic_Display.pin5, atmega328P1.D9_(PWM)
  N11: Graphic_Display.pin6, atmega328P1.D10_(PWM)
  N12: Graphic_Display.pin7, atmega328P1.D11_(PWM)
  N13: Graphic_Display.pin8, atmega328P1.D4
  N14: Graphic_Display.pin9, atmega328P1.D5_(PWM)
  N15: Graphic_Display.pin10, atmega328P1.D6_(PWM)
  N16: Graphic_Display.pin11, atmega328P1.D7
  N17: Graphic_Display.pin12, atmega328P1.A0
  N18: Graphic_Display.pin13, atmega328P1.A1
  N19: Graphic_Display.pin15, atmega328P1.A2
  N20: Graphic_Display.pin16, atmega328P1.A3
  N21: Graphic_Display.pin17, atmega328P1.A4
  N22: ICL1.CAP+, C3.1
  N23: ICL1.CAP-, C3.0
  N24: ICL1.V+, R1.wiper
  N25: atmega328P1.RESET, S1.Pin_1, S1.Pin_2, R2.Pin_0
  N26: atmega328P1.D0_(RX), J1.pin1
  N27: atmega328P1.D1_(TX), J1.pin2

notes:
  1
  20
  EN
  D / I
  R / W
  CS 1 / 2
  gbMon2 lcdBridge
  5V Rot
  Noch Platz für 3 LEDs
  Parts List:
  1x ATmega328p-pu
  1x ICL7660
  1x Pushbutton
  1x Crystal 16MHz
  2x Capacitor 10uF
  2x Capacitor 22pF
  1x Potentionmeter 10k Ohm
  1x Resistor 220 Ohm
  1x Pin Header Female 2x1
  1x Pin Header Male 20x1
  Direkt an Raspberry Pi angeschlossen
  3V Rot gestrichelt
  5V Rot
  Parts List:
  1x RF 434Mhz Transmitter
  1x DHT22 Temp + Humidity Sensor
  5x DS18b20 Temperature Sensor
  1x Resistor 10k Ohm
  1x Resistor 4,7k Ohm
  gbMon2 ioBridge
  6x Pushbutton

custom parts:
  atmega328P: Atmel ATmega328P microcontroller.
  RF 434Mhz Transmitter: RF 434Mhz Transmitter with 3 PINs internal antenna
